# Fritzing sketch turbidimeter_fritzing (saved by Fritzing 0.8.7b)
breadboards: 1

parts:
  IC1 = atmega328 [package=dip]
  Q = CRYSTAL [package=hc49us]
  IC2 = 74HC595 [package="DIP16 [THT]"]
  VR = Voltage Regulator [package=to-220-alt]
  C1 = Electrolytic Capacitor [capacitance=10μF package="0605 [SMD, electrolytic]"]
  C2 = Electrolytic Capacitor [capacitance=10μF package="0605 [SMD, electrolytic]"]
  R4 = Resistor [tolerance=±5% resistance=22k package=THT]
  C4 = Ceramic Capacitor [capacitance=22pF voltage=50V package="0603 [SMD, multilayer]"]
  C5 = Ceramic Capacitor [capacitance=22pF voltage=50V package="0603 [SMD, multilayer]"]
  C6 = Ceramic Capacitor [capacitance=22pF voltage=50V package="0603 [SMD, multilayer]"]
  R5 = Resistor [tolerance=±1% resistance=100 package=THT]
  R6 = Resistor [tolerance=±1% resistance=100 package=THT]
  R7 = Resistor [tolerance=±1% resistance=100 package=THT]
  R9 = Resistor [tolerance=±1% resistance=220 package=THT]
  L2 = 7-SEGMENT-4DIGIT [package=7-segment-4digit-youngsun]
  IC3 = IC, DIP package, 8 pins [chip_label=IC]
  L1 = LTE-302 [package=lte-302]
  C7 = Ceramic Capacitor [capacitance=0.1nF voltage=50V package="0603 [SMD, multilayer]"]
  BATT = 4 x AAA Battery Mount
  S2 = Round Pushbutton
  C3 = Ceramic Capacitor [capacitance=22pF voltage=50V package="0603 [SMD, multilayer]"]
  R8 = Resistor [tolerance=±1% resistance=100 package=THT]
  R1 = Resistor [tolerance=±5% resistance=2.2k package=THT]
  R2 = Resistor [tolerance=±1% resistance=10k package=THT]
  R3 = Resistor [tolerance=±1% resistance=1k package=THT]
  S1 = SWITCH_SPDT [package=kps-1290]

nets:
  N1: IC1.RESET, R4.Pin_0
  N2: IC1.D4, IC3.pin6
  VCC: IC1.VCC, IC1.AVCC, IC2.MR, IC2.VCC, VR.OUT, C2.+, R4.Pin_1, C6.0, IC3.pin5, IC3.pin7, C7.0, S2.leg0, C3.0, R2.Pin_1
  N3: IC1.GND#7, IC2.GND, IC2.OE, VR.IN, C1.-, C2.-, IC3.pin3, IC3.pin4, IC3.pin8, L1.C, C7.1, BATT.-, C3.1, R1.Pin_0, R3.Pin_0
  N4: IC1.XLAT1, Q.1, C4.1
  N5: IC1.XLAT2, Q.2, C5.1
  N6: IC1.D6_(PWM), IC2.SH_CP
  N7: IC1.D7, IC2.ST_CP
  N8: IC1.D8, IC2.DS
  N9: IC1.D11_(PWM), IC3.pin1
  N10: IC1.D12, IC3.pin2
  N11: IC1.D13, R9.Pin_1
  N12: IC1.GND#21, C6.1
  N13: IC1.A0, R5.Pin_1
  N14: IC1.A1, R6.Pin_1
  N15: IC1.A2, R7.Pin_1
  N16: IC1.A3, R8.Pin_1
  N17: IC1.A4, R2.Pin_0, R3.Pin_1
  N18: IC1.A5, S2.leg1, R1.Pin_1
  N19: IC2.Q1, L2.1
  N20: IC2.Q2, L2.9
  N21: IC2.Q3, L2.8
  N22: IC2.Q5, L2.4
  N23: IC2.Q6, L2.10
  N24: IC2.Q0, L2.5
  N25: VR.GND, C1.+, S1.P, S1.S
  N26: C4.0, C5.0
  N27: R5.Pin_0, L2.11
  N28: R6.Pin_0, L2.2
  N29: R7.Pin_0, L2.3
  N30: R9.Pin_0, L1.A
  N31: L2.6, R8.Pin_0
  N32: BATT.+, S1.O
